// Logisim project pong.circ as structural Verilog: 1 circuit, main circuit main
module main (
);

  wire and_1_out, and_2_out, and_3_out, and_4_out, and_5_out, and_8_out, and_9_out, block_storage_1_p5,
       BSRead, BusReq, clock_1_out, clock_2_out, clock_3_out, clock_5_out, comparator_1_eq, comparator_2_eq,
       comparator_3_eq, comparator_4_eq, comparator_5_eq, comparator_6_eq, comparator_7_eq, comparator_8_eq,
       DMAMemRead, DMAMemWrite, ExternalIntReq, keyboard_1_avail, MemRead, MemWrite, por_1_out, RAMRead,
       rgb_video_1_p2, rgb_video_1_p3, rv32im_cpu_1_p8, rv32im_cpu_1_p9, rv32im_cpu_1_p10, timer_1_p4,
       TimerIntReq;
  wire [3:0] DMABE, multiplexer_5_out, undriven;
  wire [6:0] keyboard_1_data;
  wire [31:0] Address, bit_extender_1_out, bit_extender_2_out, DMAAddress, DMAWData, multiplexer_6_out,
       multiplexer_7_out, multiplexer_8_out, multiplexer_9_out, multiplexer_10_out, ram_1_dout, RData,
       rom_1_data, rv32im_cpu_1_p6, rv32im_cpu_1_p7, timer_1_p6, WData;

  Clock clock_1 (.out(clock_1_out));
  Clock clock_2 (.out(clock_2_out));
  Comparator #(.width(32)) comparator_1 (.a(Address), .b(32'hffff000c), .eq(comparator_1_eq));  // open: gt, lt
  and and_1 (and_1_out, comparator_1_eq, MemWrite);
  // RV32IM_CPU #(.hexRegisters("true")) rv32im_cpu_1: pin names not known; wires that end beside it: clock_1_out, RData, TimerIntReq, ExternalIntReq, BusReq, rv32im_cpu_1_p6, rv32im_cpu_1_p7, rv32im_cpu_1_p8, rv32im_cpu_1_p9, rv32im_cpu_1_p10
  TTY #(.cols(80), .rows(12)) tty_1 (.data(WData[6:0]), .clk(clock_2_out), .we(and_1_out));  // open: clr
  Comparator #(.width(32)) comparator_2 (.a(Address), .b(32'hffff0008), .eq(comparator_2_eq));  // open: gt, lt
  Clock clock_3 (.out(clock_3_out));
  Keyboard keyboard_1 (
    .clk(clock_3_out), .re(and_2_out), .avail(keyboard_1_avail), .data(keyboard_1_data));  // open: clr
  and and_2 (and_2_out, comparator_2_eq, MemRead);
  Comparator #(.width(32)) comparator_3 (.a(Address), .b(32'hffff0004), .eq(comparator_3_eq));  // open: gt, lt
  assign bit_extender_1_out = {{25{1'b0}}, keyboard_1_data};  // Bit_Extender bit_extender_1
  assign bit_extender_2_out = {{31{1'b0}}, keyboard_1_avail};  // Bit_Extender bit_extender_2
  and and_3 (and_3_out, comparator_3_eq, MemRead);
  Multiplexer #(.width(32)) multiplexer_1 (
    .in0(rv32im_cpu_1_p6), .in1(DMAAddress), .out(Address), .sel(rv32im_cpu_1_p10));
  Multiplexer #(.width(32)) multiplexer_2 (.in0(rv32im_cpu_1_p7), .in1(DMAWData), .out(WData), .sel(rv32im_cpu_1_p10));
  Multiplexer multiplexer_3 (.in0(rv32im_cpu_1_p8), .in1(DMAMemRead), .out(MemRead), .sel(rv32im_cpu_1_p10));
  Multiplexer multiplexer_4 (.in0(rv32im_cpu_1_p9), .in1(DMAMemWrite), .out(MemWrite), .sel(rv32im_cpu_1_p10));
  Multiplexer #(.width(4)) multiplexer_5 (.in0(undriven), .in1(DMABE), .out(multiplexer_5_out), .sel(rv32im_cpu_1_p10));
  Multiplexer #(.width(32)) multiplexer_6 (
    .in0({32{1'b0}}), .in1(bit_extender_1_out), .out(multiplexer_6_out), .sel(and_2_out));
  Multiplexer #(.width(32)) multiplexer_7 (
    .in0(multiplexer_6_out), .in1(bit_extender_2_out), .out(multiplexer_7_out), .sel(and_3_out));
  Comparator #(.mode("unsigned"), .width(12)) comparator_4 (
    .a(Address[31:20]), .b(12'h1), .eq(comparator_4_eq));  // open: gt, lt
  Comparator #(.mode("unsigned"), .width(16)) comparator_5 (
    .a(Address[31:16]), .b(16'h200), .eq(comparator_5_eq));  // open: gt, lt
  // Timer timer_1: pin names not known; wires that end beside it: Address, MemRead, MemWrite, timer_1_p4, WData, timer_1_p6, TimerIntReq
  Clock clock_4 (.out(timer_1_p4));
  Comparator #(.mode("unsigned"), .width(16)) comparator_6 (
    .a(Address[31:16]), .b({16{1'b0}}), .eq(comparator_6_eq));  // open: gt, lt
  and and_4 (and_4_out, comparator_6_eq, MemRead);
  and and_5 (and_5_out, MemWrite, comparator_4_eq);
  and and_6 (RAMRead, comparator_4_eq, MemRead);
  and and_7 (BSRead, MemRead, comparator_7_eq);
  Comparator #(.mode("unsigned"), .width(24)) comparator_7 (
    .a(Address[31:8]), .b(24'h2000), .eq(comparator_7_eq));  // open: gt, lt
  and and_8 (and_8_out, comparator_7_eq, MemWrite);
  and and_9 (and_9_out, MemRead, comparator_5_eq);
  Multiplexer #(.width(32)) multiplexer_8 (
    .in0(multiplexer_7_out), .in1(timer_1_p6), .out(multiplexer_8_out), .sel(and_9_out));
  ROM #(.addrWidth(14), .dataWidth(32)) rom_1 (.addr(Address[15:2]), .data(rom_1_data));
  RAM #(.addrWidth(18), .asyncread("true"), .byteenables("byteEnables"), .dataWidth(32)) ram_1 (
    .addr(Address[19:2]), .we(and_5_out), .oe(RAMRead), .clk(clock_5_out), .din(WData), .dout(ram_1_dout),
    .be3(multiplexer_5_out[3]), .be2(multiplexer_5_out[2]), .be1(multiplexer_5_out[1]),
    .be0(multiplexer_5_out[0]));
  Clock clock_5 (.out(clock_5_out));
  // Block_Storage block_storage_1: pin names not known; wires that end beside it: BSRead, and_8_out, WData, rv32im_cpu_1_p10, block_storage_1_p5, DMAWData, RData, DMAMemRead, DMAMemWrite, DMAAddress, BusReq
  Clock clock_6 (.out(block_storage_1_p5));
  POR #(.PorHighDuration(1)) por_1 (.out(por_1_out));
  // RGB_Video #(.cursor("No Cursor"), .height(32), .scale(8), .width(32)) rgb_video_1: pin names not known; wires that end beside it: por_1_out, rgb_video_1_p2, rgb_video_1_p3, Address[6:2], Address[11:7]
  Clock clock_7 (.out(rgb_video_1_p2));
  Comparator #(.width(20)) comparator_8 (.a(20'hffff8), .b(Address[31:12]), .eq(comparator_8_eq));  // open: gt, lt
  and and_10 (rgb_video_1_p3, comparator_8_eq, MemWrite);
  Multiplexer #(.width(32)) multiplexer_9 (
    .in0(multiplexer_8_out), .in1(rom_1_data), .out(multiplexer_9_out), .sel(and_4_out));
  Multiplexer #(.width(32)) multiplexer_10 (
    .in0(multiplexer_9_out), .in1(ram_1_dout), .out(multiplexer_10_out), .sel(RAMRead));
  Multiplexer #(.width(32)) multiplexer_11 (.in0(multiplexer_10_out), .in1(DMAWData), .out(RData), .sel(BSRead));

  // Notes on the sheet:
  //   Display:
  //   Keyboard:
  //   BusAck 0: CPU, 1: DMA
  //   Read chain: 0, or the data of the device that is read
  //   contents of rom_1 (hex, n*v repeats v):
  //   110117 ffc10113 513 593 613 38000ef 6f 54783 78e63 ffff0737 c70713 150513 f72023 54783 fe079ae3 8067
  //   ffff07b7 47a503 8067 fd010113 2112623 2812423 2912223 3212023 1312e23 1412c23 1512a23 1612823
  //   1712623 1812423 1912223 a00793 100737 f72223 100737 f72023 1007b7 7a423 ffff8737 10007b7 fff78793
  //   52f72423 23400513 f71ff0ef fff00493 100413 100a37 1009b7 1f00913 1000b37 9b0b33 100ab7 200b93
  //   440006f 17aa423 c93 ffff07b7 47a783 2078863 ffff07b7 87a783 ffff0737 f72623 fd078693 900713 cd76c63
  //   2c9713 1970733 171713 e68cb3 4a2603 8606b3 9a783 978733 d97663 408606b3 40800433 e97663 40978733
  //   409004b3 579793 c787b3 279793 ffff8637 c787b3 7a023 571793 d787b3 279793 c787b3 167a023 da2223
  //   e9a023 8aa783 100713 2e78263 f77780e3 f8079ae3 ffff0737 472703 f80704e3 100713 eaa423 78c13 ffff07b7
  //   47a783 f60788e3 ffff07b7 87a783 ffff0737 f72623 fd078693 900713 f0d76ae3 2c1713 1870733 171713
  //   e68c33 f41ff06f aa423 1894463 1995863 25400513 e31ff0ef f29ff06f 9a783 579793 4a2703 e787b3 279793
  //   ffff8737 e787b3 7a023 5c9793 18787b3 279793 e787b3 167a023 18a2223 199a023 ee9ff06f 75706e69
  //   656e2074 6f632077 7364726f 20736120 3c592c58 65746e45 a3e72 2077654e 726f6f63 6f207364 6f207475
  //   6f622066 73646e75 a21
endmodule
