// Logisim project pong_interrupt.circ as structural Verilog: 1 circuit, main circuit main
module main (
);

  wire and_1_out, and_2_out, and_3_out, and_4_out, and_5_out, and_8_out, and_9_out, block_storage_1_p5,
       BSRead, BusReq, clock_1_out, clock_2_out, clock_3_out, clock_5_out, comparator_1_eq, comparator_2_eq,
       comparator_3_eq, comparator_4_eq, comparator_5_eq, comparator_6_eq, comparator_7_eq, comparator_8_eq,
       DMAMemRead, DMAMemWrite, ExternalIntReq, MemRead, MemWrite, por_1_out, RAMRead, rgb_video_1_p2,
       rgb_video_1_p3, rv32im_cpu_1_p8, rv32im_cpu_1_p9, rv32im_cpu_1_p10, timer_1_p4, TimerIntReq;
  wire [3:0] DMABE, multiplexer_5_out, undriven;
  wire [6:0] keyboard_1_data;
  wire [31:0] Address, bit_extender_1_out, bit_extender_2_out, DMAAddress, DMAWData, multiplexer_6_out,
       multiplexer_7_out, multiplexer_8_out, multiplexer_9_out, multiplexer_10_out, ram_1_dout, RData,
       rom_1_data, rv32im_cpu_1_p6, rv32im_cpu_1_p7, timer_1_p6, WData;

  Clock clock_1 (.out(clock_1_out));
  Clock clock_2 (.out(clock_2_out));
  Comparator #(.width(32)) comparator_1 (.a(Address), .b(32'hffff000c), .eq(comparator_1_eq));  // open: gt, lt
  and and_1 (and_1_out, comparator_1_eq, MemWrite);
  // RV32IM_CPU #(.hexRegisters("true")) rv32im_cpu_1: pin names not known; wires that end beside it: clock_1_out, RData, TimerIntReq, ExternalIntReq, BusReq, rv32im_cpu_1_p6, rv32im_cpu_1_p7, rv32im_cpu_1_p8, rv32im_cpu_1_p9, rv32im_cpu_1_p10
  TTY #(.cols(80), .rows(12)) tty_1 (.data(WData[6:0]), .clk(clock_2_out), .we(and_1_out));  // open: clr
  Comparator #(.width(32)) comparator_2 (.a(Address), .b(32'hffff0008), .eq(comparator_2_eq));  // open: gt, lt
  Clock clock_3 (.out(clock_3_out));
  Keyboard keyboard_1 (.clk(clock_3_out), .re(and_2_out), .avail(ExternalIntReq), .data(keyboard_1_data));  // open: clr
  and and_2 (and_2_out, comparator_2_eq, MemRead);
  Comparator #(.width(32)) comparator_3 (.a(Address), .b(32'hffff0004), .eq(comparator_3_eq));  // open: gt, lt
  assign bit_extender_1_out = {{25{1'b0}}, keyboard_1_data};  // Bit_Extender bit_extender_1
  assign bit_extender_2_out = {{31{1'b0}}, ExternalIntReq};  // Bit_Extender bit_extender_2
  and and_3 (and_3_out, comparator_3_eq, MemRead);
  Multiplexer #(.width(32)) multiplexer_1 (
    .in0(rv32im_cpu_1_p6), .in1(DMAAddress), .out(Address), .sel(rv32im_cpu_1_p10));
  Multiplexer #(.width(32)) multiplexer_2 (.in0(rv32im_cpu_1_p7), .in1(DMAWData), .out(WData), .sel(rv32im_cpu_1_p10));
  Multiplexer multiplexer_3 (.in0(rv32im_cpu_1_p8), .in1(DMAMemRead), .out(MemRead), .sel(rv32im_cpu_1_p10));
  Multiplexer multiplexer_4 (.in0(rv32im_cpu_1_p9), .in1(DMAMemWrite), .out(MemWrite), .sel(rv32im_cpu_1_p10));
  Multiplexer #(.width(4)) multiplexer_5 (.in0(undriven), .in1(DMABE), .out(multiplexer_5_out), .sel(rv32im_cpu_1_p10));
  Multiplexer #(.width(32)) multiplexer_6 (
    .in0({32{1'b0}}), .in1(bit_extender_1_out), .out(multiplexer_6_out), .sel(and_2_out));
  Multiplexer #(.width(32)) multiplexer_7 (
    .in0(multiplexer_6_out), .in1(bit_extender_2_out), .out(multiplexer_7_out), .sel(and_3_out));
  Comparator #(.mode("unsigned"), .width(12)) comparator_4 (
    .a(Address[31:20]), .b(12'h1), .eq(comparator_4_eq));  // open: gt, lt
  Comparator #(.mode("unsigned"), .width(16)) comparator_5 (
    .a(Address[31:16]), .b(16'h200), .eq(comparator_5_eq));  // open: gt, lt
  // Timer timer_1: pin names not known; wires that end beside it: Address, MemRead, MemWrite, timer_1_p4, WData, timer_1_p6, TimerIntReq
  Clock clock_4 (.out(timer_1_p4));
  Comparator #(.mode("unsigned"), .width(16)) comparator_6 (
    .a(Address[31:16]), .b({16{1'b0}}), .eq(comparator_6_eq));  // open: gt, lt
  and and_4 (and_4_out, comparator_6_eq, MemRead);
  and and_5 (and_5_out, MemWrite, comparator_4_eq);
  and and_6 (RAMRead, comparator_4_eq, MemRead);
  and and_7 (BSRead, MemRead, comparator_7_eq);
  Comparator #(.mode("unsigned"), .width(24)) comparator_7 (
    .a(Address[31:8]), .b(24'h2000), .eq(comparator_7_eq));  // open: gt, lt
  and and_8 (and_8_out, comparator_7_eq, MemWrite);
  and and_9 (and_9_out, MemRead, comparator_5_eq);
  Multiplexer #(.width(32)) multiplexer_8 (
    .in0(multiplexer_7_out), .in1(timer_1_p6), .out(multiplexer_8_out), .sel(and_9_out));
  ROM #(.addrWidth(14), .dataWidth(32)) rom_1 (.addr(Address[15:2]), .data(rom_1_data));
  RAM #(.addrWidth(18), .asyncread("true"), .byteenables("byteEnables"), .dataWidth(32)) ram_1 (
    .addr(Address[19:2]), .we(and_5_out), .oe(RAMRead), .clk(clock_5_out), .din(WData), .dout(ram_1_dout),
    .be3(multiplexer_5_out[3]), .be2(multiplexer_5_out[2]), .be1(multiplexer_5_out[1]),
    .be0(multiplexer_5_out[0]));
  Clock clock_5 (.out(clock_5_out));
  // Block_Storage block_storage_1: pin names not known; wires that end beside it: BSRead, and_8_out, WData, rv32im_cpu_1_p10, block_storage_1_p5, DMAWData, RData, DMAMemRead, DMAMemWrite, DMAAddress, BusReq
  Clock clock_6 (.out(block_storage_1_p5));
  POR #(.PorHighDuration(1)) por_1 (.out(por_1_out));
  // RGB_Video #(.cursor("No Cursor"), .height(32), .scale(8), .width(32)) rgb_video_1: pin names not known; wires that end beside it: por_1_out, rgb_video_1_p2, rgb_video_1_p3, Address[6:2], Address[11:7]
  Clock clock_7 (.out(rgb_video_1_p2));
  Comparator #(.width(20)) comparator_8 (.a(20'hffff8), .b(Address[31:12]), .eq(comparator_8_eq));  // open: gt, lt
  and and_10 (rgb_video_1_p3, comparator_8_eq, MemWrite);
  Multiplexer #(.width(32)) multiplexer_9 (
    .in0(multiplexer_8_out), .in1(rom_1_data), .out(multiplexer_9_out), .sel(and_4_out));
  Multiplexer #(.width(32)) multiplexer_10 (
    .in0(multiplexer_9_out), .in1(ram_1_dout), .out(multiplexer_10_out), .sel(RAMRead));
  Multiplexer #(.width(32)) multiplexer_11 (.in0(multiplexer_10_out), .in1(DMAWData), .out(RData), .sel(BSRead));

  // Notes on the sheet:
  //   Display:
  //   Keyboard:
  //   BusAck 0: CPU, 1: DMA
  //   Read chain: 0, or the data of the device that is read
  //   contents of rom_1 (hex, n*v repeats v):
  //   110117 ffc10113 513 593 613 1d0000ef 6f ff010113 112623 1007b7 5907a703 fe00793 6e7f263 ffff07b7
  //   47a783 ffff06b7 868693 ffff0737 470713 78863 6a783 72783 fe079ce3 3d4000ef c12083 1010113 8067
  //   1007b7 5907a703 1007b7 78793 e787b3 78023 1007b7 100713 58e7aa23 fa5ff06f ffff07b7 47a783 f8078ce3
  //   ffff0837 880813 ffff05b7 c58593 a00e13 1006b7 fe00e93 100337 30313 ffff08b7 488893 82703 e5a023
  //   f9c70ce3 5906a783 f8fee8e3 178613 58c6a823 f307b3 e78023 8a783 fc079ce3 f3dff06f ff010113 112623
  //   1005b7 58593 1c00793 10f5a423 58c58793 10f5a223 10058593 39800513 248000ef 1537 80050513 248000ef
  //   254000ef c12083 1010113 8067 54783 78e63 ffff0737 c70713 150513 f72023 54783 fe079ae3 8067 1007b7
  //   5907a703 ff00793 6e7e463 1007b7 78793 f70733 10078893 513 100613 40f60633 900813 e605b3 74683
  //   fd068793 2f86663 251793 a787b3 179793 fd068693 f68533 170713 fd171ce3 1007b7 58b7a823 8067 1007b7
  //   58b7a823 8067 513 8067 fd010113 2112623 2812423 2912223 3212023 1312e23 1412c23 1512a23 1612823
  //   1712623 1812423 100437 a00793 58f42e23 1004b7 58f4ac23 4b800513 f1dff0ef 1007b7 5807a823 1007b7
  //   5807aa23 ec1ff0ef 5984a783 579793 59c42703 e787b3 279793 ffff8737 e787b3 1000737 fff70713 e7a023
  //   fff00a13 100993 40913 1f00a93 ffff8437 70b13 4d800b93 500006f 5984a783 579793 59c92703 e787b3 279793
  //   8787b3 7a023 551793 18787b3 279793 8787b3 167a023 59892e23 58a4ac23 1007b7 5807a823 1007b7 5807aa23
  //   b8000ef 59c92603 13606b3 5984a783 1478733 daf663 413606b3 413009b3 eaf663 41478733 41400a33 579793
  //   c787b3 279793 8787b3 7a023 571793 d787b3 279793 8787b3 167a023 58d92e23 58e4ac23 64000ef 1007b7
  //   5947a783 f8078ce3 1007b7 5807a823 e25ff0ef 50c13 e1dff0ef 20c2793 78663 2052793 f20796e3 b8513
  //   de1ff0ef f59ff06f 30551073 34059073 8067 30451073 8067 30402573 8067 30046073 8067 30047073 8067
  //   34051573 152a23 252c23 352e23 2452023 2552223 2652423 2752623 2852823 2952a23 2b52e23 4c52023
  //   4d52223 4e52423 4f52623 5052823 5152a23 5252c23 5352e23 7452023 7552223 7652423 7752623 7852823
  //   7952a23 7a52c23 7b52e23 9c52023 9d52223 9e52423 9f52623 340022f3 2552c23 452103 852283 28067
  //   34202573 8067 3852283 34029073 1452083 1852103 1c52183 2052203 2452283 2852303 2c52383 3052403
  //   3452483 3c52583 4052603 4452683 4852703 4c52783 5052803 5452883 5852903 5c52983 6052a03 6452a83
  //   6852b03 6c52b83 7052c03 7452c83 7852d03 7c52d83 8052e03 8452e83 8852f03 8c52f83 34051573 30200073
  //   75706e69 656e2074 6f632077 7364726f 20736120 3c592c58 65746e45 a3e72 2077654e 726f6f63 6f207364
  //   6f207475 6f622066 73646e75 a21
endmodule
