// Logisim project computer.circ as structural Verilog: 1 circuit, main circuit main
module main (
);

  wire and_1_out, and_2_out, and_3_out, and_4_out, and_5_out, and_8_out, and_9_out, block_storage_1_p5,
       BSRead, BusReq, clock_1_out, clock_2_out, clock_3_out, clock_4_out, comparator_1_eq, comparator_2_eq,
       comparator_3_eq, comparator_4_eq, comparator_5_eq, comparator_6_eq, comparator_7_eq, DMAMemRead,
       DMAMemWrite, ExternalIntReq, keyboard_1_avail, MemRead, MemWrite, RAMRead, rv32im_cpu_1_p8,
       rv32im_cpu_1_p9, rv32im_cpu_1_p10, TimerIntReq;
  wire [3:0] DMABE, multiplexer_5_out, undriven;
  wire [6:0] keyboard_1_data;
  wire [31:0] Address, bit_extender_1_out, bit_extender_2_out, DMAAddress, DMAWData, multiplexer_6_out,
       multiplexer_7_out, multiplexer_8_out, multiplexer_9_out, multiplexer_10_out, ram_1_dout, RData,
       rom_1_data, rv32im_cpu_1_p6, rv32im_cpu_1_p7, timer_1_p5, WData;

  Clock clock_1 (.out(clock_1_out));
  Clock clock_2 (.out(clock_2_out));
  Comparator #(.width(32)) comparator_1 (.a(Address), .b(32'hffff000c), .eq(comparator_1_eq));  // open: gt, lt
  and and_1 (and_1_out, comparator_1_eq, MemWrite);
  // RV32IM_CPU #(.hexRegisters("true")) rv32im_cpu_1: pin names not known; wires that end beside it: clock_1_out, RData, TimerIntReq, ExternalIntReq, BusReq, rv32im_cpu_1_p6, rv32im_cpu_1_p7, rv32im_cpu_1_p8, rv32im_cpu_1_p9, rv32im_cpu_1_p10
  TTY #(.cols(80), .rows(12)) tty_1 (.data(WData[6:0]), .clk(clock_2_out), .we(and_1_out));  // open: clr
  Comparator #(.width(32)) comparator_2 (.a(Address), .b(32'hffff0008), .eq(comparator_2_eq));  // open: gt, lt
  Clock clock_3 (.out(clock_3_out));
  Keyboard keyboard_1 (
    .clk(clock_3_out), .re(and_2_out), .avail(keyboard_1_avail), .data(keyboard_1_data));  // open: clr
  and and_2 (and_2_out, comparator_2_eq, MemRead);
  Comparator #(.width(32)) comparator_3 (.a(Address), .b(32'hffff0004), .eq(comparator_3_eq));  // open: gt, lt
  assign bit_extender_1_out = {{25{1'b0}}, keyboard_1_data};  // Bit_Extender bit_extender_1
  assign bit_extender_2_out = {{31{1'b0}}, keyboard_1_avail};  // Bit_Extender bit_extender_2
  and and_3 (and_3_out, comparator_3_eq, MemRead);
  Multiplexer #(.width(32)) multiplexer_1 (
    .in0(rv32im_cpu_1_p6), .in1(DMAAddress), .out(Address), .sel(rv32im_cpu_1_p10));
  Multiplexer #(.width(32)) multiplexer_2 (.in0(rv32im_cpu_1_p7), .in1(DMAWData), .out(WData), .sel(rv32im_cpu_1_p10));
  Multiplexer multiplexer_3 (.in0(rv32im_cpu_1_p8), .in1(DMAMemRead), .out(MemRead), .sel(rv32im_cpu_1_p10));
  Multiplexer multiplexer_4 (.in0(rv32im_cpu_1_p9), .in1(DMAMemWrite), .out(MemWrite), .sel(rv32im_cpu_1_p10));
  Multiplexer #(.width(4)) multiplexer_5 (.in0(undriven), .in1(DMABE), .out(multiplexer_5_out), .sel(rv32im_cpu_1_p10));
  Multiplexer #(.width(32)) multiplexer_6 (
    .in0({32{1'b0}}), .in1(bit_extender_1_out), .out(multiplexer_6_out), .sel(and_2_out));
  Multiplexer #(.width(32)) multiplexer_7 (
    .in0(multiplexer_6_out), .in1(bit_extender_2_out), .out(multiplexer_7_out), .sel(and_3_out));
  Comparator #(.mode("unsigned"), .width(12)) comparator_4 (
    .a(Address[31:20]), .b(12'h1), .eq(comparator_4_eq));  // open: gt, lt
  Comparator #(.mode("unsigned"), .width(16)) comparator_5 (
    .a(Address[31:16]), .b(16'h200), .eq(comparator_5_eq));  // open: gt, lt
  // Timer timer_1: pin names not known; wires that end beside it: Address, MemRead, MemWrite, WData, timer_1_p5, TimerIntReq
  Comparator #(.mode("unsigned"), .width(16)) comparator_6 (
    .a(Address[31:16]), .b({16{1'b0}}), .eq(comparator_6_eq));  // open: gt, lt
  and and_4 (and_4_out, comparator_6_eq, MemRead);
  and and_5 (and_5_out, MemWrite, comparator_4_eq);
  and and_6 (RAMRead, comparator_4_eq, MemRead);
  and and_7 (BSRead, MemRead, comparator_7_eq);
  Comparator #(.mode("unsigned"), .width(24)) comparator_7 (
    .a(Address[31:8]), .b(24'h2000), .eq(comparator_7_eq));  // open: gt, lt
  and and_8 (and_8_out, comparator_7_eq, MemWrite);
  and and_9 (and_9_out, MemRead, comparator_5_eq);
  Multiplexer #(.width(32)) multiplexer_8 (
    .in0(multiplexer_7_out), .in1(timer_1_p5), .out(multiplexer_8_out), .sel(and_9_out));
  ROM #(.addrWidth(14), .dataWidth(32)) rom_1 (.addr(Address[15:2]), .data(rom_1_data));
  RAM #(.addrWidth(18), .asyncread("true"), .byteenables("byteEnables"), .dataWidth(32)) ram_1 (
    .addr(Address[19:2]), .we(and_5_out), .oe(RAMRead), .clk(clock_4_out), .din(WData), .dout(ram_1_dout),
    .be3(multiplexer_5_out[3]), .be2(multiplexer_5_out[2]), .be1(multiplexer_5_out[1]),
    .be0(multiplexer_5_out[0]));
  Clock clock_4 (.out(clock_4_out));
  // Block_Storage block_storage_1: pin names not known; wires that end beside it: BSRead, and_8_out, WData, rv32im_cpu_1_p10, block_storage_1_p5, DMAWData, RData, DMAMemRead, DMAMemWrite, DMAAddress, BusReq
  Clock clock_5 (.out(block_storage_1_p5));
  Multiplexer #(.width(32)) multiplexer_9 (
    .in0(multiplexer_8_out), .in1(rom_1_data), .out(multiplexer_9_out), .sel(and_4_out));
  Multiplexer #(.width(32)) multiplexer_10 (
    .in0(multiplexer_9_out), .in1(ram_1_dout), .out(multiplexer_10_out), .sel(RAMRead));
  Multiplexer #(.width(32)) multiplexer_11 (.in0(multiplexer_10_out), .in1(DMAWData), .out(RData), .sel(BSRead));

  // Notes on the sheet:
  //   Display:
  //   Keyboard:
  //   BusAck 0: CPU, 1: DMA
  //   Read chain: 0, or the data of the device that is read
  //   contents of rom_1 (hex, n*v repeats v):
  //   200117 ffc10113 513 593 613 38000ef 6f ffff07b7 a7a623 8067 54783 78e63 ffff0737 c70713 f72023
  //   150513 54783 fe079ae3 8067 ff010113 112623 517 1c50513 fcdff0ef 513 c12083 1010113 8067 6c6c6548
  //   6f77206f 21646c72 a
endmodule
